# Fritzing sketch diagram (saved by Fritzing 0.9.3b)
breadboards: 1

parts:
  LCD2 = LCD screen
  LCM1602_IIC2 = LCM1602 IIC [part_number="LCM1602 IIC" chip_label="LCM1602 IIC" package="DIP (Dual Inline) [THT]"]
  Mod1 = KY-018 Photoresistor Module [package="Breakout board"]
  Mod2 = KY-008 Laser Transmitter Module [package="Breakout board"]
  A1 = WeMos D1 R1
  BAT1 = BC9VPC [package=bc9vpc]
  Mod3 = KY-019 5V Relay Module [package="Breakout board"]
  Part1 = Arduino Uno (Rev3) - ICSP

nets:
  VSS: LCD2.VSS, LCM1602_IIC2.VSS
  VDD: LCD2.VDD, LCM1602_IIC2.VDD
  N1: LCD2.V0, LCM1602_IIC2.V0
  N2: LCD2.RS, LCM1602_IIC2.RS
  N3: LCD2.R/W, LCM1602_IIC2.RW
  N4: LCD2.E, LCM1602_IIC2.E
  N5: LCD2.DB0, LCM1602_IIC2.D0
  N6: LCD2.DB1, LCM1602_IIC2.D1
  N7: LCD2.DB2, LCM1602_IIC2.D2
  N8: LCD2.DB3, LCM1602_IIC2.D3
  N9: LCD2.DB4, LCM1602_IIC2.D4
  N10: LCD2.DB5, LCM1602_IIC2.D5
  N11: LCD2.DB6, LCM1602_IIC2.D6
  N12: LCD2.DB7, LCM1602_IIC2.D7
  N13: LCD2.LED+, LCM1602_IIC2.A
  N14: LCD2.LED-, LCM1602_IIC2.K
  N15: LCM1602_IIC2.GND, Mod1.-, Mod2.-, A1.Pin_13, A1.Pin_65, A1.Pin_66, BAT1.V-
  VCC: LCM1602_IIC2.VCC, Mod1.Vin, Mod2.S, Mod2.NC, A1.Pin_15, Mod3.Common
  N16: LCM1602_IIC2.SDA, A1.Pin_25, A1.Pin_45
  N17: LCM1602_IIC2.SCL, Mod1.S, A1.Pin_27, A1.Pin_43
  N18: LCM1602_IIC2.LED_A, LCM1602_IIC2.LED_B
  N19: BAT1.V+, Mod3.NO
  N20: Mod3.S, Part1.D2
  N21: Mod3.+, Part1.5V
  N22: Mod3.-, Part1.GND

custom parts:
  LCM1602 IIC: I2C-Module to use a 1602 or 2004 LCD on with the wire.h libory Serial LCD Modul
  KY-018 Photoresistor Module: KY-018 Photoresistor module, used to measure light intensity. It can determine the presence or absence of light.
  KY-008 Laser Transmitter Module: KY-008 Laser Transmitter Module, emits a dot shaped red laser beam.
  WeMos D1 R1: The WeMos D1 is a ESP8266 WiFi based board that uses the Arduino layout with a operating voltage of 3.3V.
  KY-019 5V Relay Module: KY-019 5V Relay module, used to control AC circuits. (Special thanks to vanepp for fixing the PCB holes and other errors)
